# Fritzing sketch mars_rover_schematic (saved by Fritzing 1.0.4)
breadboards: 3

parts:
  A1 = Raspberry Pi 5  # not connected
  Part1 = Adafruit 16-Channel PWM + Servo HAT [part_number="Adafruit #2327"]
  M1 = DC Motor [voltage_(max)=7.2V voltage_(min)=3V]
  SERVO1 = Servo
  M7 = MDD10A
  M8 = MDD10A
  M9 = MDD10A
  M10 = DC Motor [voltage_(max)=7.2V voltage_(min)=3V]
  M11 = DC Motor [voltage_(max)=7.2V voltage_(min)=3V]
  M12 = DC Motor [voltage_(max)=7.2V voltage_(min)=3V]
  M13 = DC Motor [voltage_(max)=7.2V voltage_(min)=3V]
  M14 = DC Motor [voltage_(max)=7.2V voltage_(min)=3V]
  DC1 = DC_DC_XL4016 [package=board_screw]
  DC2 = DC_DC_XL4016 [package=board_screw]
  SERVO2 = Servo
  SERVO3 = Servo
  SERVO4 = Servo
  BAT1 = Lithium Ion Polymer Battery 11.1v 5000mah
  BAT2 = Lithium Ion Polymer Battery 11.1v 5000mah
  Power_plug1 = USB-C plug
  J1 = Power Jack [package=power_jack_pth]
  BAT3 = Lithium Ion Polymer Battery 11.1v 5000mah

nets:
  N1: Part1.#7, SERVO4.Signal
  N2: Part1.#6, SERVO3.Signal
  N3: Part1.#5, SERVO2.Signal
  N4: Part1.#4, SERVO1.Signal
  N5: Part1.#3, M7.DIR2
  N6: Part1.#2, M7.PWM1
  N7: Part1.#1, M7.PWM2
  N8: Part1.#0, M7.DIR1
  N9: Part1.#15, M8.PWM2
  N10: Part1.#14, M8.DIR2
  N11: Part1.#13, M8.DIR1
  N12: Part1.#12, M8.PWM1
  N13: Part1.#11, M9.DIR1
  N14: Part1.#10, M9.PWM1
  N15: Part1.#9, M9.DIR2
  N16: Part1.#8, M9.PWM2
  N17: M1.pin_1, M7.M1B-1
  N18: M1.pin_2, M7.M1A1
  +5V: SERVO1.+5V, DC2.OUT+, SERVO2.+5V, SERVO3.+5V, SERVO4.+5V
  GND: SERVO1.GND, DC2.OUT-, SERVO2.GND, SERVO3.GND, SERVO4.GND
  N19: M7.Bat+, M8.Bat+, M9.Bat+, DC1.IN+, DC2.IN+, BAT1.positive, BAT2.positive, BAT3.positive
  GND_2: M7.Bat-, M7.GND, M8.Bat-, M8.GND, M9.Bat-, M9.GND, DC1.IN-, DC2.IN-, BAT1.negative, BAT2.negative, BAT3.negative
  N20: M7.M2A-1, M12.pin_2
  N21: M7.M2B-1, M12.pin_1
  N22: M8.M1B-1, M10.pin_1
  N23: M8.M1A1, M10.pin_2
  N24: M8.M2A-1, M13.pin_2
  N25: M8.M2B-1, M13.pin_1
  N26: M9.M1B-1, M11.pin_1
  N27: M9.M1A1, M11.pin_2
  N28: M9.M2A-1, M14.pin_2
  N29: M9.M2B-1, M14.pin_1
  N30: DC1.OUT+, Power_plug1.VCC
  N31: DC1.OUT-, Power_plug1.GND
  N32: J1.GND, J1.GNDBREAK

notes:
  7.4 V 5.2 Ah battery
  buck converter, set to 7.4 V- 5 V
  buck converter set to decided servo motor voltage (5-8 V)
  motor driver
  PWM hat for Raspberry Pi

custom parts:
  Raspberry Pi 5: The RPi5, a faster version of the awesome Raspberry Pi4B ARM Board with 40 pin gpio.
  Adafruit 16-Channel PWM + Servo HAT: The Raspberry Pi is a wonderful little computer, but one thing it isn't very good at is controlling DC Servo Motors - these motors need very specific and repetitive timing pulses to set the position. Instead of asking the Pi Linux kernel to send these signals, pop on this handy HAT! It adds the capability to control 16 Servos with perfect timing. It can also do PWM up to 1.6 KHz with 12 bit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
  USB-C plug: power plug
